# Fritzing sketch 4D_Pteranodon (saved by Fritzing 0.9.2b)
breadboards: 1

parts:
  Raspberry_Pi1 = Raspberry Pi 2
  IC1 = L293D [package=THT]
  S1 = Pushbutton [package="[THT]"]
  S2 = Pushbutton [package="[THT]"]
  VCC1 = Battery
  M2 = DC Motor

nets:
  N1: Raspberry_Pi1.GPIO17, S1.Pin_3, S1.Pin_4
  N2: Raspberry_Pi1.GPIO9, S2.Pin_3, S2.Pin_4
  N3: Raspberry_Pi1.GND, IC1.0V, S1.Pin_1, S1.Pin_2, S2.Pin_1, S2.Pin_2, VCC1.-
  N4: Raspberry_Pi1.GPIO25, IC1.+V
  N5: Raspberry_Pi1.GPIO24, IC1.In_4
  N6: Raspberry_Pi1.GPIO23, IC1.In_3
  N7: Raspberry_Pi1.5V, IC1.Enable_2
  N8: IC1.+Vmotor, VCC1.+
  N9: IC1.Out_3_(_Controlled_by_Enable_2_), M2.pin_1
  N10: IC1.Out_4_(_Controlled_by_Enable_2_), M2.pin_2
